// Logisim project Logisim_Guia04_01.circ as structural Verilog: 1 circuit, main circuit main
module main (
  input  x,
  input  y,
  input  z,
  input  x_2,
  input  y_2,
  input  z_2,
  input  x_3,
  input  y_3,
  input  z_3,
  input  x_4,
  input  y_4,
  input  z_4,
  input  x_5,
  input  y_5,
  input  z_5,
  input  x_6,
  input  y_6,
  input  z_6,
  input  x_7,
  input  y_7,
  input  z_7,
  input  y_8,
  input  z_8,
  output out_24,
  output out_25,
  output out_26,
  output out_27,
  output out_28,
  output out_29,
  output out_30,
  output out_31
);

  wire and_1_out, and_2_out, not_1_out, not_2_out, not_3_out, not_4_out, not_5_out, not_6_out, not_7_out,
       not_8_out, not_9_out, not_10_out, not_11_out, not_12_out, not_13_out, not_14_out, not_15_out,
       or_1_out, or_2_out, or_3_out, or_4_out, or_5_out, or_6_out;

  not not_1 (not_1_out, x);
  not not_2 (not_2_out, z);
  not not_3 (not_3_out, x_2);
  not not_4 (not_4_out, y_2);
  not not_5 (not_5_out, x_3);
  or or_1 (or_1_out, not_5_out, not_6_out);
  not not_6 (not_6_out, y_3);
  and and_1 (and_1_out, x_4, y_4);
  not not_7 (not_7_out, x_5);
  not not_8 (not_8_out, z_5);
  not not_9 (not_9_out, y_6);
  not not_10 (not_10_out, z_8);
  and and_2 (and_2_out, y, not_2_out);
  or or_2 (or_2_out, not_4_out, z_2);
  not not_11 (not_11_out, or_1_out);
  and and_3 (out_27, and_1_out, z_4);
  or or_3 (or_3_out, not_7_out, y_5);
  or or_4 (or_4_out, x_6, not_9_out);
  not not_12 (not_12_out, x_7);
  not not_13 (not_13_out, y_7);
  and and_4 (out_31, y_8, not_10_out);
  and and_5 (out_24, not_1_out, and_2_out);
  and and_6 (out_25, not_3_out, not_14_out);
  not not_14 (not_14_out, or_2_out);
  and and_7 (out_26, not_11_out, z_3);
  and and_8 (out_28, or_3_out, not_8_out);
  and and_9 (out_29, or_4_out, z_6);
  or or_5 (or_5_out, not_12_out, y_7);
  or or_6 (or_6_out, not_13_out, z_7);
  not not_15 (not_15_out, or_6_out);
  and and_10 (out_30, or_5_out, not_15_out);

  // Notes on the sheet:
  //   GUIA04
  //   01) a)
  //   b) (x' + y')' . z
  //   c) (x . y')' . z'
  //   d) (x' . y)' . z
  //   e) (x' + y) . (y' + z)'
  //   x' . (y' + z)'
  //   Duas formas diferentes que obtém o mesmo resultado
endmodule
