// Logisim project Logisim_Guia04_02.circ as structural Verilog: 1 circuit, main circuit main
module main (
  input  x,
  input  y,
  input  x_2,
  input  y_2,
  input  y_3,
  input  in_6,
  input  x_3,
  input  y_4,
  input  x_4,
  input  y_5,
  input  x_5,
  input  y_6,
  input  x_6,
  input  y_7,
  input  x_7,
  input  y_8,
  input  x_8,
  input  y_9,
  input  x_9,
  input  y_10,
  output out_21,
  output out_22,
  output out_23,
  output out_24,
  output out_25,
  output out_26,
  output out_27,
  output out_28,
  output out_29,
  output out_30
);

  wire and_3_out, and_4_out, nand_1_out, nor_1_out, nor_2_out, not_1_out, not_2_out, not_3_out, not_4_out,
       not_5_out, not_6_out, not_7_out, not_8_out, not_9_out, not_10_out, not_11_out, not_12_out, not_13_out,
       not_14_out, not_15_out, or_2_out, or_3_out, or_5_out, or_7_out;

  not not_1 (not_1_out, y_2);
  not not_2 (not_2_out, y_3);
  not not_3 (not_3_out, y_3);
  not not_4 (not_4_out, x_3);
  not not_5 (not_5_out, x_4);
  or or_1 (out_26, x_5, y_6);
  not not_6 (not_6_out, x_6);
  not not_7 (not_7_out, x_6);
  not not_8 (not_8_out, y_8);
  not not_9 (not_9_out, x_8);
  not not_10 (not_10_out, y_9);
  not not_11 (not_11_out, x_9);
  and and_1 (out_30, not_11_out, y_10);
  not not_12 (not_12_out, x);
  or or_2 (or_2_out, not_12_out, y);
  and and_2 (out_22, x_2, not_1_out);
  or or_3 (or_3_out, not_2_out, in_6);
  and and_3 (and_3_out, not_3_out, in_6);
  or or_4 (out_24, not_4_out, y_4);
  and and_4 (and_4_out, not_5_out, not_13_out);
  not not_13 (not_13_out, y_5);
  or or_5 (or_5_out, x_4, y_5);
  nand nand_1 (nand_1_out, not_6_out, y_7);
  nor nor_1 (nor_1_out, not_7_out, y_7);
  or or_6 (out_28, x_7, not_8_out);
  or or_7 (or_7_out, not_9_out, y_9);
  nor nor_2 (nor_2_out, not_10_out, x_8);
  not not_14 (not_14_out, or_2_out);
  or or_8 (out_23, or_3_out, and_3_out);
  not not_15 (not_15_out, and_4_out);
  and and_5 (out_25, not_15_out, or_5_out);
  or or_9 (out_27, nand_1_out, nor_1_out);
  and and_6 (out_29, or_7_out, nor_2_out);
  and and_7 (out_21, not_14_out, x);

  // Notes on the sheet:
  //   GUIA04
  //   x
  //   02) a) x . (x' + y)'  ==  x . y'
  //   b) (x' + y) + (x' . y)  ==  x' + y
  //   c) (x' . y')' . (x+y)  ==  x + y
  //   d) (x' . y)' + (x' + y)'  ==  y' + x
  //   e) (y + x') . (y' + x)'  ==  x' . y
endmodule
