// Logisim project Guia_0501.circ as structural Verilog: 1 circuit, main circuit main
module main (
  input  a,
  input  a_2,
  input  b,
  input  b_2,
  output out_5
);

  wire nor_1_out, nor_2_out, nor_3_out;

  nor nor_1 (nor_1_out, a, a_2);
  nor nor_2 (nor_2_out, b, b_2);
  nor nor_3 (nor_3_out, nor_1_out, nor_2_out);
  nor nor_4 (out_5, nor_3_out, nor_3_out);
endmodule
