// Logisim project Guia_0502.circ as structural Verilog: 1 circuit, main circuit main
module main (
  input  a,
  input  b,
  output out_3
);

  wire nand_1_out;

  nand nand_1 (nand_1_out, a, a);
  nand nand_2 (out_3, nand_1_out, b);
endmodule
