// Logisim project Guia_0601.circ as structural Verilog: 1 circuit, main circuit main
module main (
  input  x,
  input  y,
  input  z,
  input  x_2,
  input  y_2,
  input  z_2,
  input  x_3,
  input  y_3,
  input  z_3,
  input  x_4,
  input  y_4,
  input  z_4,
  input  x_5,
  input  y_5,
  input  z_5,
  input  x_6,
  input  y_6,
  input  z_6,
  output s1,
  output s2,
  output s1_2,
  output s2_2,
  output s1_3,
  output s2_3,
  output s1_4,
  output s2_4,
  output s1_5,
  output s2_5
);

  wire and_1_out, and_2_out, and_3_out, and_4_out, and_5_out, and_6_out, and_7_out, and_8_out, and_9_out,
       and_10_out, and_11_out, and_12_out, and_13_out, and_14_out, and_15_out, and_16_out, and_17_out,
       and_18_out, and_19_out, and_20_out, and_21_out, and_22_out, and_23_out, and_24_out, and_25_out,
       and_26_out, and_27_out, and_28_out, and_29_out, and_30_out, not_1_out, not_2_out, not_3_out,
       not_4_out, not_5_out, not_6_out, not_7_out, not_8_out, not_9_out, not_10_out, not_11_out, not_12_out,
       not_13_out, not_14_out, not_15_out, not_16_out, not_17_out, not_18_out, not_19_out, not_20_out,
       not_21_out, not_22_out, not_23_out, not_24_out, not_25_out, not_26_out, not_27_out, not_28_out,
       not_29_out, not_30_out, not_31_out, not_32_out, not_33_out, not_34_out, not_35_out;

  not not_1 (not_1_out, x_4);
  not not_2 (not_2_out, z_4);
  not not_3 (not_3_out, y_4);
  not not_4 (not_4_out, z_4);
  not not_5 (not_5_out, x);
  not not_6 (not_6_out, y);
  not not_7 (not_7_out, z);
  not not_8 (not_8_out, x_2);
  not not_9 (not_9_out, y_2);
  not not_10 (not_10_out, x_3);
  and and_1 (and_1_out, not_10_out, y_3, not_11_out);
  not not_11 (not_11_out, z_3);
  and and_2 (and_2_out, x_3, not_12_out, not_13_out);
  not not_12 (not_12_out, y_3);
  not not_13 (not_13_out, z_3);
  and and_3 (and_3_out, x_3, y_3, not_14_out);
  not not_14 (not_14_out, z_3);
  and and_4 (and_4_out, y_3, not_15_out);
  not not_15 (not_15_out, z_3);
  and and_5 (and_5_out, x_3, not_15_out);
  not not_16 (not_16_out, x_4);
  and and_6 (and_6_out, not_16_out, not_17_out, z_4);
  not not_17 (not_17_out, y_4);
  and and_7 (and_7_out, not_1_out, y_4, not_2_out);
  and and_8 (and_8_out, x_4, not_3_out, z_4);
  and and_9 (and_9_out, x_4, y_4, not_4_out);
  not not_18 (not_18_out, y_4);
  and and_10 (and_10_out, not_18_out, z_4);
  and and_11 (and_11_out, y_4, not_19_out);
  not not_19 (not_19_out, z_4);
  not not_20 (not_20_out, x_5);
  not not_21 (not_21_out, y_5);
  not not_22 (not_22_out, x_5);
  not not_23 (not_23_out, z_5);
  not not_24 (not_24_out, y_5);
  not not_25 (not_25_out, z_5);
  not not_26 (not_26_out, y_5);
  and and_12 (and_12_out, x_5, not_27_out);
  not not_27 (not_27_out, y_5);
  and and_13 (and_13_out, not_27_out, z_5);
  not not_28 (not_28_out, x_5);
  and and_14 (and_14_out, not_28_out, y_5, not_29_out);
  not not_29 (not_29_out, z_5);
  not not_30 (not_30_out, x_6);
  not not_31 (not_31_out, y_6);
  not not_32 (not_32_out, z_6);
  not not_33 (not_33_out, x_6);
  not not_34 (not_34_out, y_6);
  not not_35 (not_35_out, z_6);
  and and_15 (and_15_out, not_5_out, not_6_out, z);
  and and_16 (and_16_out, x, y, not_7_out);
  and and_17 (and_17_out, x, y, z);
  and and_18 (and_18_out, not_8_out, not_9_out, z_2);
  and and_19 (and_19_out, x_2, y_2);
  or or_1 (s2_2, and_4_out, and_5_out);
  or or_2 (s1_3, and_6_out, and_7_out, and_8_out, and_9_out);
  or or_3 (s2_3, and_10_out, and_11_out);
  and and_20 (and_20_out, not_20_out, not_21_out, z_5);
  and and_21 (and_21_out, not_22_out, y_5, not_23_out);
  and and_22 (and_22_out, x_5, not_24_out, not_25_out);
  and and_23 (and_23_out, x_5, not_26_out, z_5);
  or or_4 (s2_4, and_12_out, and_13_out, and_14_out);
  and and_24 (and_24_out, not_30_out, not_31_out, not_32_out);
  and and_25 (and_25_out, not_30_out, y_6, z_6);
  and and_26 (and_26_out, x_6, y_6, not_32_out);
  and and_27 (and_27_out, x_6, y_6, z_6);
  and and_28 (and_28_out, x_6, y_6);
  and and_29 (and_29_out, y_6, z_6);
  and and_30 (and_30_out, not_33_out, not_34_out, not_35_out);
  or or_5 (s1, and_15_out, and_16_out, and_17_out);
  or or_6 (s2, and_18_out, and_19_out);
  or or_7 (s1_2, and_1_out, and_2_out, and_3_out);
  or or_8 (s1_4, and_20_out, and_21_out, and_22_out, and_23_out);
  or or_9 (s1_5, and_24_out, and_25_out, and_26_out, and_27_out);
  or or_10 (s2_5, and_28_out, and_29_out, and_30_out);

  // Notes on the sheet:
  //   01)
  //   a)
  //   b)
  //   c)
  //   d)
  //   e)
endmodule
