// Logisim project Guia_0602.circ as structural Verilog: 1 circuit, main circuit main
module main (
  input  x,
  input  y,
  input  z,
  input  x_2,
  input  y_2,
  input  z_2,
  input  x_3,
  input  y_3,
  input  z_3,
  input  x_4,
  input  y_4,
  input  z_4,
  input  x_5,
  input  y_5,
  input  z_5,
  output out_16,
  output out_17,
  output s1,
  output s2,
  output s1_2,
  output s2_2,
  output s1_3,
  output s2_3,
  output s1_4,
  output s2_4
);

  wire not_1_out, not_2_out, not_3_out, not_4_out, not_5_out, not_6_out, not_7_out, not_8_out, not_9_out,
       not_10_out, not_11_out, not_12_out, not_13_out, not_14_out, not_15_out, not_16_out, not_17_out,
       not_18_out, not_19_out, not_20_out, not_21_out, not_22_out, not_23_out, not_24_out, not_25_out,
       not_26_out, not_27_out, not_28_out, not_29_out, or_1_out, or_2_out, or_3_out, or_4_out, or_5_out,
       or_6_out, or_7_out, or_8_out, or_9_out, or_10_out, or_11_out, or_12_out, or_13_out, or_14_out,
       or_15_out, or_16_out, or_17_out, or_18_out, or_19_out, or_20_out, or_21_out, or_22_out, or_23_out,
       or_24_out, or_25_out, or_26_out, or_27_out, or_28_out;

  not not_1 (not_1_out, z);
  not not_2 (not_2_out, x);
  not not_3 (not_3_out, y);
  or or_1 (or_1_out, y, not_4_out);
  not not_4 (not_4_out, z);
  not not_5 (not_5_out, x);
  or or_2 (or_2_out, not_5_out, not_4_out);
  not not_6 (not_6_out, x_2);
  not not_7 (not_7_out, y_2);
  not not_8 (not_8_out, x_2);
  not not_9 (not_9_out, z_3);
  not not_10 (not_10_out, y_3);
  not not_11 (not_11_out, x_3);
  or or_3 (or_3_out, y_3, not_12_out);
  not not_12 (not_12_out, z_3);
  or or_4 (or_4_out, x_3, not_13_out);
  not not_13 (not_13_out, y_3);
  not not_14 (not_14_out, y_4);
  not not_15 (not_15_out, z_4);
  not not_16 (not_16_out, x_4);
  not not_17 (not_17_out, y_4);
  not not_18 (not_18_out, z_4);
  not not_19 (not_19_out, y_5);
  not not_20 (not_20_out, y_5);
  not not_21 (not_21_out, z_5);
  not not_22 (not_22_out, x_5);
  not not_23 (not_23_out, y_5);
  not not_24 (not_24_out, x_5);
  not not_25 (not_25_out, y_5);
  not not_26 (not_26_out, z_5);
  not not_27 (not_27_out, y_5);
  not not_28 (not_28_out, x_5);
  not not_29 (not_29_out, y_5);
  or or_5 (or_5_out, x, y, not_1_out);
  or or_6 (or_6_out, not_2_out, y, not_1_out);
  or or_7 (or_7_out, not_2_out, not_3_out, not_1_out);
  and and_1 (out_17, or_1_out, or_2_out);
  or or_8 (or_8_out, x_2, y_2, z_2);
  or or_9 (or_9_out, not_6_out, y_2, z_2);
  or or_10 (or_10_out, not_6_out, not_7_out, z_2);
  or or_11 (or_11_out, y_2, z_2);
  and and_2 (s2, or_11_out, or_12_out);
  or or_12 (or_12_out, not_8_out, z_2);
  or or_13 (or_13_out, x_3, y_3, not_9_out);
  or or_14 (or_14_out, x_3, not_10_out, z_3);
  or or_15 (or_15_out, x_3, not_10_out, not_9_out);
  or or_16 (or_16_out, not_11_out, y_3, not_9_out);
  and and_3 (s2_2, or_3_out, or_4_out);
  or or_17 (or_17_out, x_4, y_4, z_4);
  or or_18 (or_18_out, x_4, not_14_out, not_15_out);
  or or_19 (or_19_out, not_16_out, y_4, z_4);
  or or_20 (or_20_out, not_16_out, not_14_out, not_15_out);
  or or_21 (or_21_out, y_4, z_4);
  or or_22 (or_22_out, not_17_out, not_18_out);
  or or_23 (or_23_out, x_5, not_19_out, z_5);
  or or_24 (or_24_out, x_5, not_20_out, not_21_out);
  or or_25 (or_25_out, not_22_out, not_23_out, z_5);
  or or_26 (or_26_out, not_24_out, not_25_out, not_26_out);
  or or_27 (or_27_out, x_5, not_27_out);
  and and_4 (s2_4, or_27_out, or_28_out);
  or or_28 (or_28_out, not_28_out, not_29_out);
  and and_5 (out_16, or_5_out, or_6_out, or_7_out);
  and and_6 (s1, or_8_out, or_9_out, or_10_out);
  and and_7 (s1_2, or_13_out, or_14_out, or_15_out, or_16_out);
  and and_8 (s1_3, or_17_out, or_18_out, or_19_out, or_20_out);
  and and_9 (s2_3, or_21_out, or_22_out);
  and and_10 (s1_4, or_23_out, or_24_out, or_25_out, or_26_out);

  // Notes on the sheet:
  //   2)
  //   a)
  //   b)
  //   c)
  //   d)
  //   e)
endmodule
