// Logisim project Guia_0604.circ as structural Verilog: 1 circuit, main circuit main
module main (
  input  x,
  input  y,
  input  w,
  input  z,
  input  x_2,
  input  y_2,
  input  w_2,
  input  z_2,
  input  x_3,
  input  y_3,
  input  w_3,
  input  z_3,
  input  x_4,
  input  y_4,
  input  w_4,
  input  z_4,
  input  x_5,
  input  y_5,
  input  w_5,
  input  z_5,
  output out_21,
  output out_22,
  output out_23,
  output out_24,
  output out_25
);

  wire not_1_out, not_2_out, not_3_out, not_4_out, not_5_out, not_6_out, not_7_out, not_8_out, not_9_out,
       not_10_out, not_11_out, not_12_out, not_13_out, not_14_out, not_15_out, not_16_out, not_17_out,
       not_18_out, not_19_out, not_20_out, or_1_out, or_2_out, or_3_out, or_4_out, or_5_out, or_6_out,
       or_7_out, or_8_out, or_9_out, or_10_out, or_11_out, or_12_out, or_13_out, or_14_out, or_15_out,
       or_16_out;

  not not_1 (not_1_out, x);
  not not_2 (not_2_out, x_2);
  not not_3 (not_3_out, x_3);
  not not_4 (not_4_out, x_4);
  not not_5 (not_5_out, x_5);
  not not_6 (not_6_out, y);
  not not_7 (not_7_out, y_2);
  not not_8 (not_8_out, y_3);
  not not_9 (not_9_out, y_4);
  not not_10 (not_10_out, y_5);
  not not_11 (not_11_out, z);
  not not_12 (not_12_out, w);
  not not_13 (not_13_out, z_2);
  not not_14 (not_14_out, w_2);
  not not_15 (not_15_out, w_3);
  not not_16 (not_16_out, z_3);
  not not_17 (not_17_out, z_4);
  not not_18 (not_18_out, w_4);
  not not_19 (not_19_out, z_5);
  not not_20 (not_20_out, w_5);
  or or_1 (or_1_out, x, not_12_out, z);
  or or_2 (or_2_out, not_6_out, not_12_out, z);
  or or_3 (or_3_out, x, not_6_out, not_12_out);
  or or_4 (or_4_out, x_2, not_7_out, w_2);
  or or_5 (or_5_out, not_2_out, w_2, not_13_out);
  or or_6 (or_6_out, not_2_out, not_7_out, not_14_out, z_2);
  or or_7 (or_7_out, not_8_out, not_15_out, not_16_out);
  or or_8 (or_8_out, not_3_out, not_8_out, not_16_out);
  or or_9 (or_9_out, x_3, not_8_out, w_3, z_3);
  or or_10 (or_10_out, not_3_out, y_3, w_3, z_3);
  or or_11 (or_11_out, x_4, w_4, not_17_out);
  or or_12 (or_12_out, not_4_out, not_9_out, not_18_out);
  or or_13 (or_13_out, not_4_out, y_4, not_17_out);
  or or_14 (or_14_out, not_10_out, not_19_out);
  or or_15 (or_15_out, x_5, not_20_out, z_5);
  or or_16 (or_16_out, not_5_out, not_20_out, not_19_out);
  and and_1 (out_22, or_4_out, or_5_out, or_6_out);
  and and_2 (out_23, or_7_out, or_8_out, or_9_out, or_10_out);
  and and_3 (out_24, or_11_out, or_12_out, or_13_out);
  and and_4 (out_25, or_14_out, or_15_out, or_16_out);
  and and_5 (out_21, or_1_out, or_2_out, or_3_out);

  // Notes on the sheet:
  //   a)
  //   b)
  //   c)
  //   d)
  //   e)
endmodule
