// Logisim project Guia_0701.circ as structural Verilog: 1 circuit, main circuit main
module main (
  input  a,
  input  b,
  input  select,
  output s
);

  wire and_1_out, and_2_out, and_3_out, nand_1_out, not_1_out;

  and and_1 (and_1_out, b, a);
  nand nand_1 (nand_1_out, b, a);
  and and_2 (and_2_out, select, and_1_out);
  not not_1 (not_1_out, select);
  and and_3 (and_3_out, not_1_out, nand_1_out);
  or or_1 (s, and_2_out, and_3_out);
endmodule
