// Logisim project Guia_0702.circ as structural Verilog: 1 circuit, main circuit main
module main (
  input  a,
  input  b,
  input  select,
  output s
);

  wire and_1_out, and_2_out, nor_1_out, not_1_out, or_1_out;

  or or_1 (or_1_out, b, a);
  nor nor_1 (nor_1_out, b, a);
  and and_1 (and_1_out, select, or_1_out);
  not not_1 (not_1_out, select);
  and and_2 (and_2_out, not_1_out, nor_1_out);
  or or_2 (s, and_1_out, and_2_out);
endmodule
