// Logisim project Guia_0704.circ as structural Verilog: 1 circuit, main circuit main
module main (
  input  a,
  input  b,
  input  select1,
  input  select2,
  output s
);

  wire and_1_out, and_2_out, and_3_out, and_4_out, and_5_out, and_6_out, nor_1_out, not_1_out, not_2_out,
       not_3_out, or_1_out, or_2_out, or_3_out, xnor_1_out, xor_1_out;

  or or_1 (or_1_out, b, a);
  xor xor_1 (xor_1_out, b, a);
  xnor xnor_1 (xnor_1_out, b, a);
  nor nor_1 (nor_1_out, b, a);
  and and_1 (and_1_out, select1, xor_1_out);
  not not_1 (not_1_out, select1);
  and and_2 (and_2_out, not_1_out, xnor_1_out);
  and and_3 (and_3_out, select1, or_1_out);
  not not_2 (not_2_out, select1);
  and and_4 (and_4_out, not_2_out, nor_1_out);
  not not_3 (not_3_out, select2);
  or or_2 (or_2_out, and_1_out, and_2_out);
  or or_3 (or_3_out, and_3_out, and_4_out);
  and and_5 (and_5_out, not_3_out, or_2_out);
  or or_4 (s, and_5_out, and_6_out);
  and and_6 (and_6_out, select2, or_3_out);
endmodule
