// Logisim project Guia_0705.circ as structural Verilog: 1 circuit, main circuit main
module main (
  input  a,
  input  b,
  input  [2:0] in_3,
  output out_4
);

  wire and_1_out, and_2_out, and_3_out, nand_1_out, nor_1_out, not_1_out, not_2_out, or_1_out, or_2_out,
       xnor_1_out, xor_1_out;

  not not_1 (not_1_out, a);
  and and_1 (and_1_out, not_1_out, not_1_out);
  and and_2 (and_2_out, not_1_out, a);
  or or_1 (or_1_out, and_1_out, and_2_out);
  and and_3 (and_3_out, b, a, or_1_out);
  nand nand_1 (nand_1_out, b, a, or_1_out);
  or or_2 (or_2_out, or_1_out, a, b);
  nor nor_1 (nor_1_out, b, a, or_1_out);
  not not_2 (not_2_out, a);
  ExactlyOne xor_1 (.out(xor_1_out), .in0(a), .in1(b), .in2(or_1_out));
  NotExactlyOne xnor_1 (.out(xnor_1_out), .in0(a), .in1(or_1_out), .in2(b));
  Multiplexer #(.select(3), .enable("false")) multiplexer_1 (
    .in0(and_3_out), .in1(nand_1_out), .in2(or_2_out), .in3(nor_1_out), .in4(xor_1_out), .in5(xnor_1_out),
    .in7(not_2_out), .out(out_4), .sel(in_3));  // open: in6
endmodule
