// Logisim project Moore_1101.circ as structural Verilog: 1 circuit, main circuit main
module main (
  input  x,
  input  reset,
  output y
);

  wire clk_out, d_ff_1_q, d_ff_2_q, d_ff_3_q, d_ff_3_qn, d_ff_4_q, d_ff_5_q;

  Clock clk (.out(clk_out));
  D_Flip_Flop d_ff_1 (.clk(clk_out), .D(x), .Q(d_ff_1_q), .reset(reset));  // open: Qn, preset
  D_Flip_Flop d_ff_2 (.clk(clk_out), .D(d_ff_1_q), .Q(d_ff_2_q), .reset(reset));  // open: Qn, preset
  D_Flip_Flop d_ff_3 (.clk(clk_out), .D(d_ff_2_q), .Q(d_ff_3_q), .Qn(d_ff_3_qn), .reset(reset));  // open: preset
  D_Flip_Flop d_ff_4 (.clk(clk_out), .D(d_ff_3_q), .Q(d_ff_4_q), .reset(reset));  // open: Qn, preset
  and and_1 (y, d_ff_5_q, d_ff_4_q, d_ff_3_qn, d_ff_2_q);
  D_Flip_Flop d_ff_5 (.clk(clk_out), .D(d_ff_4_q), .Q(d_ff_5_q), .reset(reset));  // open: Qn, preset
endmodule
