// Logisim project Guia_1201.circ as structural Verilog: 1 circuit, main circuit main
module main (
  input  addr,
  input  r_w,
  input  x,
  input  clr,
  output out_5,
  output out_6,
  output out_7,
  output out_8
);

  wire and_1_out, clk_out, j_k_ff_1_q, j_k_ff_1_qn, j_k_ff_2_q, j_k_ff_2_qn, j_k_ff_3_q, j_k_ff_3_qn,
       j_k_ff_4_q, not_1_out, not_2_out, not_3_out, not_4_out, not_5_out;

  Clock clk (.out(clk_out));
  and and_1 (and_1_out, addr, r_w, clk_out);
  not not_1 (not_1_out, x);
  J_K_Flip_Flop j_k_ff_1 (
    .J(x), .clk(and_1_out), .K(not_1_out), .Q(j_k_ff_1_q), .Qn(j_k_ff_1_qn), .reset(clr));  // open: preset
  not not_2 (not_2_out, j_k_ff_1_q);
  Multiplexer #(.enable("false")) multiplexer_1 (.in0(j_k_ff_1_q), .in1(not_2_out), .out(out_5), .sel(addr));
  J_K_Flip_Flop j_k_ff_2 (
    .J(j_k_ff_1_q), .clk(and_1_out), .K(j_k_ff_1_qn), .Q(j_k_ff_2_q), .Qn(j_k_ff_2_qn), .reset(clr));  // open: preset
  not not_3 (not_3_out, j_k_ff_2_q);
  Multiplexer #(.enable("false")) multiplexer_2 (.in0(j_k_ff_2_q), .in1(not_3_out), .out(out_6), .sel(addr));
  J_K_Flip_Flop j_k_ff_3 (
    .J(j_k_ff_2_q), .clk(and_1_out), .K(j_k_ff_2_qn), .Q(j_k_ff_3_q), .Qn(j_k_ff_3_qn), .reset(clr));  // open: preset
  not not_4 (not_4_out, j_k_ff_3_q);
  Multiplexer #(.enable("false")) multiplexer_3 (.in0(j_k_ff_3_q), .in1(not_4_out), .out(out_7), .sel(addr));
  J_K_Flip_Flop j_k_ff_4 (
    .J(j_k_ff_3_q), .clk(and_1_out), .K(j_k_ff_3_qn), .Q(j_k_ff_4_q), .reset(clr));  // open: Qn, preset
  not not_5 (not_5_out, j_k_ff_4_q);
  Multiplexer #(.enable("false")) multiplexer_4 (.in0(j_k_ff_4_q), .in1(not_5_out), .out(out_8), .sel(addr));
endmodule
