// Logisim project Guia_1301.circ as structural Verilog: 1 circuit, main circuit main
module main (
  input  x,
  input  reset
);

  wire clk_out, j_k_ff_1_qn, j_k_ff_2_qn, j_k_ff_3_qn, j_k_ff_4_qn, j_k_ff_5_qn;

  Clock clk (.out(clk_out));
  // Probe on j_k_ff_1_qn
  J_K_Flip_Flop j_k_ff_1 (.J(x), .clk(j_k_ff_2_qn), .K(x), .Qn(j_k_ff_1_qn), .reset(reset));  // open: Q, preset
  J_K_Flip_Flop j_k_ff_2 (.J(x), .clk(j_k_ff_3_qn), .K(x), .Qn(j_k_ff_2_qn), .reset(reset));  // open: Q, preset
  // Probe on j_k_ff_2_qn
  // Probe on j_k_ff_3_qn
  J_K_Flip_Flop j_k_ff_3 (.J(x), .clk(j_k_ff_4_qn), .K(x), .Qn(j_k_ff_3_qn), .reset(reset));  // open: Q, preset
  // Probe on j_k_ff_4_qn
  J_K_Flip_Flop j_k_ff_4 (.J(x), .clk(j_k_ff_5_qn), .K(x), .Qn(j_k_ff_4_qn), .reset(reset));  // open: Q, preset
  J_K_Flip_Flop j_k_ff_5 (.J(x), .clk(clk_out), .K(x), .Qn(j_k_ff_5_qn), .reset(reset));  // open: Q, preset
  // Probe on j_k_ff_5_qn

  // Notes on the sheet:
  //   contador assíncrono decrescente de 5 bits
endmodule
