// Logisim project Guia_1304.circ as structural Verilog: 1 circuit, main circuit main
module main (
  input  x,
  input  reset
);

  wire and_1_out, and_2_out, clk_out, j_k_ff_1_q, j_k_ff_1_qn, j_k_ff_2_q, j_k_ff_2_qn, j_k_ff_3_q,
       j_k_ff_3_qn, j_k_ff_4_q, j_k_ff_4_qn, nand_1_out, or_1_out;

  Clock clk (.out(clk_out));
  or or_1 (or_1_out, reset, and_1_out);
  and and_1 (and_1_out, nand_1_out, and_2_out);
  and and_2 (and_2_out, j_k_ff_1_qn, j_k_ff_3_qn);
  J_K_Flip_Flop j_k_ff_1 (
    .J(x), .clk(clk_out), .K(x), .Q(j_k_ff_1_q), .Qn(j_k_ff_1_qn), .reset(or_1_out));  // open: preset
  nand nand_1 (nand_1_out, j_k_ff_2_qn, j_k_ff_4_qn);
  // Probe on j_k_ff_4_q
  // Probe on j_k_ff_3_q
  J_K_Flip_Flop j_k_ff_2 (
    .J(x), .clk(j_k_ff_1_q), .K(x), .Q(j_k_ff_2_q), .Qn(j_k_ff_2_qn), .reset(or_1_out));  // open: preset
  // Probe on j_k_ff_2_q
  J_K_Flip_Flop j_k_ff_3 (
    .J(x), .clk(j_k_ff_2_q), .K(x), .Q(j_k_ff_3_q), .Qn(j_k_ff_3_qn), .reset(or_1_out));  // open: preset
  // Probe on j_k_ff_1_q
  J_K_Flip_Flop j_k_ff_4 (
    .J(x), .clk(j_k_ff_3_q), .K(x), .Q(j_k_ff_4_q), .Qn(j_k_ff_4_qn), .reset(or_1_out));  // open: preset

  // Notes on the sheet:
  //   contador assíncrono decádico decrescente de 4 bits
endmodule
