// Logisim project Guia_1305.circ as structural Verilog: 1 circuit, main circuit main
module main (
  input  x,
  input  reset
);

  wire and_1_out, clk_out, j_k_ff_1_q, j_k_ff_2_q, j_k_ff_3_q;

  Clock clk (.out(clk_out));
  J_K_Flip_Flop j_k_ff_1 (.J(clk_out), .clk(x), .K(x), .Q(j_k_ff_1_q), .reset(reset));  // open: Qn, preset
  // Probe on j_k_ff_1_q
  J_K_Flip_Flop j_k_ff_2 (
    .J(clk_out), .clk(j_k_ff_1_q), .K(j_k_ff_1_q), .Q(j_k_ff_2_q), .reset(reset));  // open: Qn, preset
  // Probe on j_k_ff_2_q
  and and_1 (and_1_out, j_k_ff_1_q, j_k_ff_2_q);
  // Probe on j_k_ff_3_q
  J_K_Flip_Flop j_k_ff_3 (
    .J(clk_out), .clk(and_1_out), .K(and_1_out), .Q(j_k_ff_3_q), .reset(reset));  // open: Qn, preset
endmodule
