// Logisim project Guia_1402.circ as structural Verilog: 1 circuit, main circuit main
module main (
  input  x,
  input  reset
);

  wire clk_out, d_ff_1_q, d_ff_2_q, d_ff_3_q, d_ff_4_q, d_ff_5_q, d_ff_6_q;

  Clock clk (.out(clk_out));
  // Probe on d_ff_1_q
  D_Flip_Flop d_ff_1 (.clk(clk_out), .D(d_ff_2_q), .Q(d_ff_1_q), .preset(reset));  // open: Qn, reset
  // Probe on d_ff_2_q
  D_Flip_Flop d_ff_2 (.clk(clk_out), .D(d_ff_3_q), .Q(d_ff_2_q), .preset(reset));  // open: Qn, reset
  // Probe on d_ff_3_q
  D_Flip_Flop d_ff_3 (.clk(clk_out), .D(d_ff_4_q), .Q(d_ff_3_q), .preset(reset));  // open: Qn, reset
  // Probe on d_ff_4_q
  D_Flip_Flop d_ff_4 (.clk(clk_out), .D(d_ff_5_q), .Q(d_ff_4_q), .preset(reset));  // open: Qn, reset
  // Probe on d_ff_5_q
  D_Flip_Flop d_ff_5 (.clk(clk_out), .D(d_ff_6_q), .Q(d_ff_5_q), .preset(reset));  // open: Qn, reset
  // Probe on d_ff_6_q
  D_Flip_Flop d_ff_6 (.clk(clk_out), .D(x), .Q(d_ff_6_q), .preset(reset));  // open: Qn, reset

  // Notes on the sheet:
  //   deslocamento para a esquerda de 6 bits 
endmodule
