// Logisim project Guia_1403.circ as structural Verilog: 1 circuit, main circuit main
module main (
  input  \input ,
  input  clear
);

  wire clock_1_out, d_ff_1_q, d_ff_2_q, d_ff_3_q, d_ff_4_q, d_ff_5_q, d_ff_6_q;

  Clock clock_1 (.out(clock_1_out));
  // OR_Gate or_1 has open pins: in0=\input , in1=\input , out=open
  // Probe on d_ff_1_q
  D_Flip_Flop d_ff_1 (.clk(clock_1_out), .D(d_ff_6_q), .Q(d_ff_1_q), .preset(clear));  // open: Qn, reset
  D_Flip_Flop d_ff_2 (.clk(clock_1_out), .D(d_ff_1_q), .Q(d_ff_2_q), .reset(clear));  // open: Qn, preset
  // Probe on d_ff_2_q
  // Probe on d_ff_3_q
  D_Flip_Flop d_ff_3 (.clk(clock_1_out), .D(d_ff_2_q), .Q(d_ff_3_q), .reset(clear));  // open: Qn, preset
  // Probe on d_ff_4_q
  D_Flip_Flop d_ff_4 (.clk(clock_1_out), .D(d_ff_3_q), .Q(d_ff_4_q), .reset(clear));  // open: Qn, preset
  // Probe on d_ff_5_q
  D_Flip_Flop d_ff_5 (.clk(clock_1_out), .D(d_ff_4_q), .Q(d_ff_5_q), .reset(clear));  // open: Qn, preset
  D_Flip_Flop d_ff_6 (.clk(clock_1_out), .D(d_ff_5_q), .Q(d_ff_6_q), .reset(clear));  // open: Qn, preset
  // Probe on d_ff_6_q

  // Notes on the sheet:
  //   deslocamento circular (Ring)
endmodule
