// Logisim project Guia_1405.circ as structural Verilog: 1 circuit, main circuit main
module main (
  input  clear,
  input  in_2,
  input  in_3,
  input  in_4,
  input  in_5,
  input  in_6,
  input  in_7,
  input  in_8
);

  wire and_1_out, and_2_out, and_3_out, and_4_out, and_5_out, and_6_out, clock_1_out, d_ff_1_q, d_ff_2_q,
       d_ff_3_q, d_ff_4_q, d_ff_5_q;

  Clock clock_1 (.out(clock_1_out));
  // Probe on d_ff_1_q
  D_Flip_Flop #(.Pre_Clr_Positions("LEGACY")) d_ff_1 (
    .clk(clock_1_out), .D(1'b0), .Q(d_ff_1_q), .preset(and_1_out), .reset(clear));  // open: Qn
  and and_1 (and_1_out, in_2, in_3);
  D_Flip_Flop #(.Pre_Clr_Positions("LEGACY")) d_ff_2 (
    .clk(clock_1_out), .D(d_ff_1_q), .Q(d_ff_2_q), .preset(and_2_out), .reset(clear));  // open: Qn
  and and_2 (and_2_out, in_2, in_4);
  // Probe on d_ff_2_q
  and and_3 (and_3_out, in_2, in_5);
  // Probe on d_ff_3_q
  D_Flip_Flop #(.Pre_Clr_Positions("LEGACY")) d_ff_3 (
    .clk(clock_1_out), .D(d_ff_2_q), .Q(d_ff_3_q), .preset(and_3_out), .reset(clear));  // open: Qn
  D_Flip_Flop #(.Pre_Clr_Positions("LEGACY")) d_ff_4 (
    .clk(clock_1_out), .D(d_ff_3_q), .Q(d_ff_4_q), .preset(and_4_out), .reset(clear));  // open: Qn
  and and_4 (and_4_out, in_2, in_6);
  // Probe on d_ff_4_q
  and and_5 (and_5_out, in_2, in_7);
  // Probe on d_ff_5_q
  D_Flip_Flop #(.Pre_Clr_Positions("LEGACY")) d_ff_5 (
    .clk(clock_1_out), .D(d_ff_4_q), .Q(d_ff_5_q), .preset(and_5_out), .reset(clear));  // open: Qn
  D_Flip_Flop #(.Pre_Clr_Positions("LEGACY")) d_ff_6 (
    .clk(clock_1_out), .D(d_ff_5_q), .preset(and_6_out), .reset(clear));  // open: Q, Qn
  and and_6 (and_6_out, in_2, in_8);
endmodule
