// Logisim project Guia_1701.circ as structural Verilog: 1 circuit, main circuit main
module main (
  input  imput,
  output out_2
);

  wire clock_out, d_ff_1_q;

  Clock clock (.out(clock_out));
  D_Flip_Flop d_ff_1 (.clk(clock_out), .D(imput), .Q(d_ff_1_q));  // open: Qn, preset, reset
  D_Flip_Flop d_ff_2 (.clk(clock_out), .D(d_ff_1_q), .Q(out_2));  // open: Qn, preset, reset
endmodule
