// Logisim project Guia_1703.circ as structural Verilog: 1 circuit, main circuit main
module main (
  input  in_1,
  input  in_2,
  output out_3
);

  wire clock_1_out, j_k_ff_1_q;

  Clock clock_1 (.out(clock_1_out));
  J_K_Flip_Flop j_k_ff_1 (.J(in_1), .clk(clock_1_out), .K(in_2), .Q(j_k_ff_1_q));  // open: Qn, preset, reset
  D_Flip_Flop d_ff_1 (.clk(clock_1_out), .D(j_k_ff_1_q), .Q(out_3));  // open: Qn, preset, reset
endmodule
