// Logisim project R01_01.circ as structural Verilog: 1 circuit, main circuit main
module main (
  input  a,
  input  b,
  input  c,
  input  d,
  input  a_2,
  input  b_2,
  input  c_2,
  input  d_2,
  input  a_3,
  input  b_3,
  input  c_3,
  input  d_3,
  input  a_4,
  input  b_4,
  input  c_4,
  input  d_4,
  input  a_5,
  input  b_5,
  input  c_5,
  input  d_5,
  input  a_6,
  input  b_6,
  input  c_6,
  input  d_6,
  output out_25,
  output out_26,
  output out_27,
  output out_28,
  output out_29,
  output out_30
);

  wire and_1_out, and_2_out, and_3_out, and_4_out, and_5_out, and_6_out, and_7_out, and_8_out, and_9_out,
       norA_out, norAC_out, norAD_out, norB_out, norBC_out, norC_out, norCD_out, norD_out, not_1_out,
       not_2_out, not_3_out, not_4_out, not_5_out, not_6_out, not_7_out, not_8_out, not_9_out, not_10_out,
       not_11_out, not_12_out, not_13_out, not_14_out, not_15_out, not_16_out, notC_out, notD_out, or_1_out,
       or_2_out, or_3_out, or_4_out, or_5_out, or_8_out, or_9_out, or_10_out, or_11_out, or_12_out,
       or_13_out, or_14_out, or_15_out, or_16_out, or_17_out, RESULT1_out, RESULT2_out, result_out,
       term1_out, term2_out, term2n_out, term3_out;

  not not_1 (not_1_out, a);
  not not_2 (not_2_out, a_3);
  not not_3 (not_3_out, a_4);
  not not_4 (not_4_out, b);
  not not_5 (not_5_out, c);
  not not_6 (not_6_out, b_3);
  not not_7 (not_7_out, c_3);
  not not_8 (not_8_out, c_4);
  not not_9 (not_9_out, b_4);
  not not_10 (not_10_out, d);
  not not_11 (not_11_out, d_3);
  not not_12 (not_12_out, d_4);
  and and_1 (and_1_out, not_1_out, b, not_5_out, not_10_out);
  and and_2 (and_2_out, a, not_4_out, not_5_out, not_10_out);
  and and_3 (and_3_out, a, not_4_out, not_5_out, d);
  and and_4 (and_4_out, a, b, not_5_out, not_10_out);
  and and_5 (and_5_out, a, b, not_5_out, d);
  and and_6 (and_6_out, a, b, c, not_10_out);
  and and_7 (and_7_out, a_3, not_7_out);
  and and_8 (and_8_out, b_3, not_7_out, not_11_out);
  and and_9 (and_9_out, a_3, b_3, not_11_out);
  or or_1 (or_1_out, a_4, b_4);
  or or_2 (or_2_out, not_8_out, not_12_out);
  or or_3 (or_3_out, b_4, not_8_out);
  or or_4 (or_4_out, a_4, not_8_out);
  or or_5 (or_5_out, a_4, not_12_out);
  // NAND_Gate nand_1 is placed but not wired
  nand notC (notC_out, c_5, c_5);
  nand notD (notD_out, d_5, d_5);
  // NOR_Gate nor_1 is placed but not wired
  nor norA (norA_out, a_6, a_6);
  nor norB (norB_out, b_6, b_6);
  nor norC (norC_out, c_6, c_6);
  nor norD (norD_out, d_6, d_6);
  nor norAB (norC_out, a_6, b_6);
  or or_6 (out_27, and_7_out, and_8_out, and_9_out);
  and and_10 (out_28, or_1_out, or_2_out, or_3_out, or_4_out, or_5_out);
  nand term1 (term1_out, notC_out, a_5);
  nand term2n (term2n_out, notC_out, b_5);
  nor norCD (norCD_out, norC_out, norD_out);
  nor norBC (norBC_out, b_6, norC_out);
  nor norAC (norAC_out, a_6, norC_out);
  nor norAD (norAD_out, a_6, norD_out);
  or or_7 (out_25, and_1_out, and_2_out, and_3_out, and_4_out, and_5_out, and_6_out);
  nand term2 (term2_out, notD_out, term2n_out);
  nand term3 (term3_out, a_5, b_5, notD_out);
  nor RESULT1 (RESULT1_out, norC_out, norCD_out);
  nor RESULT2 (RESULT2_out, norBC_out, norAC_out, norAD_out);
  not not_13 (not_13_out, a_2);
  not not_14 (not_14_out, b_2);
  nand result (result_out, term1_out, term2_out, term3_out);
  or SAIDA (out_30, RESULT1_out, RESULT2_out);
  not not_15 (not_15_out, c_2);
  not not_16 (not_16_out, d_2);
  nand \final  (out_29, result_out, result_out);
  or or_8 (or_8_out, a_2, b_2, c_2, d_2);
  or or_9 (or_9_out, a_2, b_2, d_2, not_16_out);
  or or_10 (or_10_out, a_2, b_2, not_15_out, d_2);
  or or_11 (or_11_out, a_2, b_2, not_15_out, not_16_out);
  or or_12 (or_12_out, a_2, not_14_out, c_2, not_16_out);
  or or_13 (or_13_out, a_2, not_14_out, not_15_out, d_2);
  or or_14 (or_14_out, a_2, not_14_out, not_15_out, not_16_out);
  or or_15 (or_15_out, not_13_out, b_2, not_15_out, d_2);
  or or_16 (or_16_out, not_13_out, b_2, not_15_out, not_16_out);
  or or_17 (or_17_out, not_13_out, not_14_out, not_15_out, not_16_out);
  and and_11 (out_26, or_8_out, or_9_out, or_10_out, or_11_out, or_12_out, or_13_out, or_14_out, or_15_out, or_16_out, or_17_out);

  // Notes on the sheet:
  //   SoP canonica
  //   SoP nand
  //   PoS nor
  //   Simplificação mintermo
  //   Simplificação maxtermo
  //   PoS canonica
endmodule
