// Logisim project R01_02.circ as structural Verilog: 1 circuit, main circuit main
module main (
  input  a,
  input  select,
  input  c,
  input  a_2,
  input  select_b,
  output out_6,
  output out_7
);

  wire multiplexer_2_out, not_1_out, not_2_out, not_3_out;

  not not_1 (not_1_out, a);
  not not_2 (not_2_out, a_2);
  Multiplexer #(.enable("false")) multiplexer_1 (.in0(a), .in1(not_1_out), .out(out_6), .sel(select));
  Multiplexer #(.enable("false")) multiplexer_2 (.in0(not_2_out), .in1(a_2), .out(multiplexer_2_out), .sel(select_b));
  not not_3 (not_3_out, c);
  Multiplexer #(.enable("false")) multiplexer_3 (.in0(not_3_out), .in1(c), .out(out_7), .sel(multiplexer_2_out));

  // Notes on the sheet:
  //   mux(a, not a, c)
  //   mux(c,not c, mux(a, not a, b))
endmodule
