// Logisim project R01_03.circ as structural Verilog: 1 circuit, main circuit main
module main (
  input  a,
  input  b,
  input  c,
  input  x,
  input  y,
  output out_6,
  output out_7
);

  wire not_1_out, not_2_out, not_3_out, or_1_out, or_2_out, or_3_out, or_4_out;

  not not_1 (not_1_out, y);
  not not_2 (not_2_out, a);
  not not_3 (not_3_out, c);
  or or_1 (or_1_out, x, not_1_out);
  or or_2 (or_2_out, x, y);
  or or_3 (or_3_out, not_2_out, b);
  or or_4 (or_4_out, b, not_3_out);
  and and_1 (out_7, or_1_out, or_2_out);
  and and_2 (out_6, or_3_out, or_4_out);

  // Notes on the sheet:
  //   (~a|b)&(b|~c)
  //   (x'y)'(x'y')' == (x+y')(x+y)
endmodule
