// Logisim project Questao01.circ as structural Verilog: 1 circuit, main circuit main
module main (
  input  a,
  input  b,
  input  c,
  input  d,
  input  a_2,
  input  b_2,
  input  c_2,
  input  d_2,
  input  a_3,
  input  b_3,
  input  c_3,
  input  d_3,
  input  a_4,
  input  b_4,
  input  c_4,
  input  d_4,
  input  a_5,
  input  b_5,
  input  c_5,
  input  d_5,
  input  a_6,
  input  b_6,
  input  c_6,
  input  d_6,
  output out_25,
  output out_26,
  output out_27,
  output out_28,
  output out_29,
  output out_30
);

  wire and_1_out, and_2_out, and_3_out, and_4_out, and_5_out, and_6_out, and_7_out, and_8_out, and_9_out,
       and_10_out, and_11_out, and_12_out, not_1_out, not_2_out, not_3_out, not_4_out, not_5_out, not_6_out,
       not_7_out, not_8_out, not_9_out, not_10_out, not_11_out, not_12_out, not_13_out, not_14_out,
       not_15_out, not_16_out, or_1_out, or_2_out, or_3_out, or_4_out, or_5_out, or_6_out, or_7_out;

  not not_1 (not_1_out, c);
  not not_2 (not_2_out, d);
  not not_3 (not_3_out, b);
  not not_4 (not_4_out, a);
  not not_5 (not_5_out, b_2);
  not not_6 (not_6_out, c_2);
  not not_7 (not_7_out, d_2);
  not not_8 (not_8_out, c_3);
  not not_9 (not_9_out, d_3);
  not not_10 (not_10_out, a_3);
  not not_11 (not_11_out, b_3);
  not not_12 (not_12_out, c_4);
  not not_13 (not_13_out, d_4);
  not not_14 (not_14_out, d_5);
  not not_15 (not_15_out, c_5);
  and and_1 (and_1_out, a, not_1_out, d);
  and and_2 (and_2_out, a, c, not_2_out);
  and and_3 (and_3_out, a, not_3_out, c);
  and and_4 (and_4_out, not_4_out, b, c, d);
  or or_1 (or_1_out, c_2, d_2);
  or or_2 (or_2_out, b_2, c_2);
  or or_3 (or_3_out, not_5_out, not_6_out, not_7_out);
  or or_4 (or_4_out, b_2, d_2);
  and and_5 (and_5_out, not_8_out, d_3);
  and and_6 (and_6_out, c_3, not_9_out);
  and and_7 (and_7_out, not_10_out, c_3);
  and and_8 (and_8_out, not_11_out, c_3);
  and and_9 (and_9_out, a_4, not_12_out, not_13_out);
  and and_10 (and_10_out, b_4, c_4, d_4);
  or or_5 (or_5_out, c_5, not_14_out);
  or or_6 (or_6_out, not_15_out, d_5);
  or or_7 (or_7_out, b_5, d_5);
  not not_16 (not_16_out, c_6);
  and and_11 (and_11_out, not_16_out, d_6);
  and and_12 (and_12_out, a_6, b_6, d_6);
  and and_13 (out_26, or_1_out, or_2_out, or_3_out, or_4_out);
  or or_8 (out_27, and_5_out, and_6_out, and_7_out, and_8_out);
  or or_9 (out_28, and_9_out, and_10_out);
  or or_10 (out_30, and_11_out, and_12_out);
  or or_11 (out_25, and_1_out, and_2_out, and_3_out, and_4_out);
  and and_14 (out_29, or_5_out, or_6_out, or_7_out);

  // Notes on the sheet:
  //   Sop(Da) = 7,9,10,11,13,14
  //   Sop(Ta) = 7,8,12,15
  //   Sop(Tc) = 1,5,9,13,15
  //   Pos(Db) = 0,1,2,4,7,8,9,10,12,15
  //   Sop(Dc) = 1,2,3,5,6,7,9,10,11,13
  //   Pos(Tb) = 0,1,2,5,6,8,9,10,13,14
endmodule
