// Logisim project Questao03.circ as structural Verilog: 1 circuit, main circuit main
module main (
  input  in_1,
  input  in_2
);

  wire a_q, b_q, clock_out, not_1_out, not_2_out;

  Clock clock (.out(clock_out));
  J_K_Flip_Flop a (.J(in_2), .clk(clock_out), .K(in_2), .Q(a_q), .preset(in_1));  // open: Qn, reset
  not not_1 (not_1_out, a_q);
  J_K_Flip_Flop b (.J(not_1_out), .clk(a_q), .K(not_1_out), .Q(b_q));  // open: Qn, preset, reset
  not not_2 (not_2_out, b_q);
  J_K_Flip_Flop c (.J(not_2_out), .clk(b_q), .K(not_2_out));  // open: Q, Qn, preset, reset
endmodule
