// Logisim project Questao04.circ as structural Verilog: 1 circuit, main circuit main
module main (
  input  in_1
);

  wire a_q, b_q, clock_out, not_1_out;

  Clock clock (.out(clock_out));
  D_Flip_Flop a (.clk(clock_out), .D(in_1), .Q(a_q));  // open: Qn, preset, reset
  not not_1 (not_1_out, b_q);
  D_Flip_Flop b (.clk(clock_out), .D(a_q), .Q(b_q));  // open: Qn, preset, reset
  D_Flip_Flop c (.clk(clock_out), .D(not_1_out));  // open: Q, Qn, preset, reset
endmodule
