// Logisim project Questao05.circ as structural Verilog: 1 circuit, main circuit main
module main (
  input  x,
  input  reset
);

  wire and_1_out, and_2_out, clk_out, nand_1_out, or_1_out, t_ff_1_q, t_ff_1_qn, t_ff_2_q, t_ff_2_qn,
       t_ff_3_q, t_ff_3_qn, t_ff_4_q;

  Clock clk (.out(clk_out));
  and and_1 (and_1_out, nand_1_out, and_2_out);
  or or_1 (or_1_out, reset, and_1_out);
  and and_2 (and_2_out, t_ff_3_q, t_ff_1_q);
  // Probe on t_ff_4_q
  T_Flip_Flop t_ff_1 (.clk(clk_out), .T(x), .Q(t_ff_1_q), .Qn(t_ff_1_qn), .reset(or_1_out));  // open: preset
  nand nand_1 (nand_1_out, t_ff_4_q, t_ff_2_q);
  // Probe on t_ff_3_q
  T_Flip_Flop t_ff_2 (.clk(t_ff_1_qn), .T(x), .Q(t_ff_2_q), .Qn(t_ff_2_qn), .reset(or_1_out));  // open: preset
  // Probe on t_ff_2_q
  T_Flip_Flop t_ff_3 (.clk(t_ff_2_qn), .T(x), .Q(t_ff_3_q), .Qn(t_ff_3_qn), .reset(or_1_out));  // open: preset
  // Probe on t_ff_1_q
  T_Flip_Flop t_ff_4 (.clk(t_ff_3_qn), .T(x), .Q(t_ff_4_q), .reset(or_1_out));  // open: Qn, preset
endmodule
