// Logisim project ULA.circ as structural Verilog
module somador (
  input  ci1,
  input  x1,
  input  y1,
  output s1,
  output co1
);

  wire meiasoma_1_co0, meiasoma_1_s0, meiasoma_2_co0;

  meiasoma meiasoma_1 (.x0(x1), .y0(y1), .co0(meiasoma_1_co0), .s0(meiasoma_1_s0));
  meiasoma meiasoma_2 (.x0(ci1), .y0(meiasoma_1_s0), .co0(meiasoma_2_co0), .s0(s1));
  or or_1 (co1, meiasoma_1_co0, meiasoma_2_co0);
endmodule

module meiasoma (
  input  x0,
  input  y0,
  output s0,
  output co0
);

  and and_1 (co0, y0, x0);
  xor xor_1 (s0, x0, y0);
endmodule

module ULA (
  input  Binvert,
  input  vem1,
  input  a,
  input  b,
  input  seletor1,
  input  seletor2,
  output s,
  output vai1
);

  wire adder_1_out, and_1_out, multiplexer_1_out, not_1_out, not_2_out, or_1_out;

  Multiplexer #(.enable("false")) multiplexer_1 (.in0(b), .in1(not_1_out), .out(multiplexer_1_out), .sel(Binvert));
  not not_1 (not_1_out, b);
  and and_1 (and_1_out, a, multiplexer_1_out);
  or or_1 (or_1_out, a, multiplexer_1_out);
  not not_2 (not_2_out, a);
  Adder #(.width(1)) adder_1 (.a(a), .b(multiplexer_1_out), .out(adder_1_out), .cin(vem1), .cout(vai1));
  mux2seletor MUX (
    .a(and_1_out), .b(or_1_out), .c(not_2_out), .d(adder_1_out), .seletor1(seletor1), .seletor2(seletor2),
    .s(s));
endmodule

module mux2seletor (
  input  a,
  input  b,
  input  c,
  input  d,
  input  seletor1,
  input  seletor2,
  output s
);

  wire and_1_out, and_2_out, and_3_out, and_4_out, not_1_out, not_2_out, not_3_out, not_4_out;

  not not_1 (not_1_out, seletor1);
  not not_2 (not_2_out, seletor2);
  not not_3 (not_3_out, seletor1);
  not not_4 (not_4_out, seletor2);
  and and_1 (and_1_out, a, not_1_out, not_2_out);
  and and_2 (and_2_out, b, not_3_out, seletor2);
  and and_3 (and_3_out, c, seletor1, not_4_out);
  and and_4 (and_4_out, d, seletor1, seletor2);
  or or_1 (s, and_1_out, and_2_out, and_3_out, and_4_out);
endmodule

module ULA4BITS (
  input  Binvert,
  input  B3,
  input  B2,
  input  B1,
  input  B0,
  input  A3,
  input  A2,
  input  A1,
  input  A0,
  input  OP0,
  input  OP1,
  output s0,
  output s1,
  output s2,
  output s3,
  output cout
);

  wire ula_2_vai1, ula_3_vai1, ULA_vai1;

  ULA ULA (.a(A0), .b(B0), .Binvert(Binvert), .vem1(Binvert), .vai1(ULA_vai1), .seletor1(OP0), .seletor2(OP1), .s(s0));
  ULA ula_2 (
    .a(A1), .b(B1), .Binvert(Binvert), .vem1(ULA_vai1), .vai1(ula_2_vai1), .seletor1(OP0), .seletor2(OP1),
    .s(s1));
  ULA ula_3 (
    .a(A2), .b(B2), .Binvert(Binvert), .vem1(ula_2_vai1), .vai1(ula_3_vai1), .seletor1(OP0), .seletor2(OP1),
    .s(s2));
  ULA ula_4 (.a(A3), .b(B3), .Binvert(Binvert), .vem1(ula_3_vai1), .vai1(cout), .seletor1(OP0), .seletor2(OP1), .s(s3));

  // Notes on the sheet:
  //   cin
endmodule
