// Logisim project AtividadePratica01.circ as structural Verilog: 5 circuits, main circuit main
module main (
  input  A0,
  input  A1,
  input  ci,
  input  A2,
  input  A3,
  input  B0,
  input  B1,
  input  B2,
  input  B3,
  output co,
  output out_11,
  output out_12,
  output out_13,
  output out_14
);

  wire decodificadorA_a, decodificadorA_b, decodificadorA_c, decodificadorA_d, decodificadorA_e,
       decodificadorA_f, decodificadorA_g, decodificadorB_a, decodificadorB_b, decodificadorB_c,
       decodificadorB_d, decodificadorB_e, decodificadorB_f, decodificadorB_g, decodificadorSOMA_a,
       decodificadorSOMA_b, decodificadorSOMA_c, decodificadorSOMA_d, decodificadorSOMA_e,
       decodificadorSOMA_f, decodificadorSOMA_g;

  decodificador decodificadorA (
    .E3(A3), .E2(A2), .E1(A1), .E0(A0), .a(decodificadorA_a), .b(decodificadorA_b), .c(decodificadorA_c),
    .d(decodificadorA_d), .e(decodificadorA_e), .f(decodificadorA_f), .g(decodificadorA_g));
  decodificador decodificadorB (
    .E3(B3), .E2(B2), .E1(B1), .E0(B0), .a(decodificadorB_a), .b(decodificadorB_b), .c(decodificadorB_c),
    .d(decodificadorB_d), .e(decodificadorB_e), .f(decodificadorB_f), .g(decodificadorB_g));
  soma4bits somador_de_4_bits (
    .x0(A0), .y0(B0), .x1(A1), .y1(B1), .x2(A2), .y2(B2), .x3(A3), .y3(B3), .ci(ci), .co(co), .s0(out_14),
    .s1(out_13), .s2(out_12), .s3(out_11));
  _7_Segment_Display u_7_segment_display_1 (
    .g(decodificadorA_g), .f(decodificadorA_f), .a(decodificadorA_a), .b(decodificadorA_b),
    .e(decodificadorA_e), .d(decodificadorA_d), .c(decodificadorA_c));  // open: dp
  _7_Segment_Display u_7_segment_display_2 (
    .g(decodificadorB_g), .f(decodificadorB_f), .a(decodificadorB_a), .b(decodificadorB_b),
    .e(decodificadorB_e), .d(decodificadorB_d), .c(decodificadorB_c));  // open: dp
  decodificador decodificadorSOMA (
    .E3(out_11), .E2(out_12), .E1(out_13), .E0(out_14), .a(decodificadorSOMA_a), .b(decodificadorSOMA_b),
    .c(decodificadorSOMA_c), .d(decodificadorSOMA_d), .e(decodificadorSOMA_e), .f(decodificadorSOMA_f),
    .g(decodificadorSOMA_g));
  _7_Segment_Display u_7_segment_display_3 (
    .g(decodificadorSOMA_g), .f(decodificadorSOMA_f), .a(decodificadorSOMA_a), .b(decodificadorSOMA_b),
    .e(decodificadorSOMA_e), .d(decodificadorSOMA_d), .c(decodificadorSOMA_c));  // open: dp

  // Notes on the sheet:
  //   Calculadora de 4 bits
  //   Autor: Alessandra Faria Rodrigues
endmodule

module meiasoma (
  input  x0,
  input  y0,
  output s0,
  output co0
);

  and and_1 (co0, y0, x0);
  xor xor_1 (s0, x0, y0);
endmodule

module somacompleta (
  input  ci1,
  input  x1,
  input  y1,
  output s1,
  output co1
);

  wire meiasoma_1_co0, meiasoma_1_s0, meiasoma_2_co0;

  meiasoma meiasoma_1 (.x0(x1), .y0(y1), .co0(meiasoma_1_co0), .s0(meiasoma_1_s0));
  meiasoma meiasoma_2 (.x0(ci1), .y0(meiasoma_1_s0), .co0(meiasoma_2_co0), .s0(s1));
  or or_1 (co1, meiasoma_1_co0, meiasoma_2_co0);
endmodule

module soma4bits (
  input  ci,
  input  x0,
  input  y0,
  input  x1,
  input  y1,
  input  x2,
  input  y2,
  input  x3,
  input  y3,
  output s0,
  output s1,
  output s2,
  output s3,
  output co
);

  wire somacompleta_1_co1, somacompleta_2_co1, somacompleta_3_co1;

  somacompleta somacompleta_1 (.x1(x0), .y1(y0), .ci1(ci), .co1(somacompleta_1_co1), .s1(s0));
  somacompleta somacompleta_2 (.x1(x1), .y1(y1), .ci1(somacompleta_1_co1), .co1(somacompleta_2_co1), .s1(s1));
  somacompleta somacompleta_3 (.x1(x2), .y1(y2), .ci1(somacompleta_2_co1), .co1(somacompleta_3_co1), .s1(s2));
  somacompleta somacompleta_4 (.x1(x3), .y1(y3), .ci1(somacompleta_3_co1), .co1(co), .s1(s3));
endmodule

module decodificador (
  input  E3,
  input  E2,
  input  E1,
  input  E0,
  output a,
  output b,
  output c,
  output d,
  output e,
  output f,
  output g
);

  wire and_1_out, and_2_out, and_3_out, and_4_out, and_5_out, and_6_out, and_7_out, and_8_out, and_9_out,
       and_10_out, and_11_out, and_12_out, and_13_out, and_14_out, and_15_out, and_16_out, and_17_out,
       and_18_out, and_19_out, and_20_out, and_21_out, and_22_out, and_23_out, and_24_out, and_25_out,
       and_26_out, and_27_out, and_28_out, and_29_out, and_30_out, and_31_out, and_32_out, and_33_out,
       and_34_out, and_35_out, and_36_out, and_37_out, and_38_out, and_39_out, and_40_out, and_41_out,
       and_42_out, and_43_out, and_44_out, and_45_out, and_46_out, and_47_out, not_1_out, not_2_out,
       not_3_out, not_4_out, not_5_out, not_6_out, not_7_out, not_8_out, not_9_out, not_10_out, not_11_out,
       not_12_out, not_13_out, not_14_out, not_15_out, not_16_out, not_17_out, not_18_out, not_19_out,
       not_20_out, not_21_out, not_22_out, not_23_out, not_24_out, not_25_out, not_26_out, not_27_out,
       not_28_out, not_29_out, not_30_out, not_31_out, not_32_out, not_33_out, not_34_out, not_35_out,
       not_36_out, not_37_out, not_38_out, not_39_out, not_40_out, not_41_out, not_42_out, not_43_out,
       not_44_out, or_1_out, or_2_out, or_3_out, or_4_out, or_5_out, or_6_out, or_7_out, or_8_out, or_9_out,
       or_10_out, or_12_out, or_13_out, or_14_out, or_15_out, or_16_out, or_17_out, or_18_out, or_20_out,
       or_21_out, or_22_out, or_23_out;

  not not_1 (not_1_out, E2);
  not not_2 (not_2_out, E0);
  not not_3 (not_3_out, E3);
  not not_4 (not_4_out, E3);
  and and_1 (and_1_out, E3, not_5_out);
  not not_5 (not_5_out, E2);
  not not_6 (not_6_out, E1);
  not not_7 (not_7_out, E3);
  not not_8 (not_8_out, E2);
  not not_9 (not_9_out, E3);
  and and_2 (and_2_out, not_9_out, not_10_out);
  not not_10 (not_10_out, E1);
  not not_11 (not_11_out, E0);
  not not_12 (not_12_out, E3);
  not not_13 (not_13_out, E1);
  not not_14 (not_14_out, E3);
  and and_3 (and_3_out, not_14_out, not_15_out);
  not not_15 (not_15_out, E1);
  not not_16 (not_16_out, E3);
  and and_4 (and_4_out, not_16_out, E0);
  not not_17 (not_17_out, E1);
  not not_18 (not_18_out, E3);
  not not_19 (not_19_out, E2);
  not not_20 (not_20_out, E3);
  and and_5 (and_5_out, not_20_out, not_21_out);
  not not_21 (not_21_out, E2);
  not not_22 (not_22_out, E0);
  not not_23 (not_23_out, E2);
  and and_6 (and_6_out, not_23_out, E1);
  not not_24 (not_24_out, E1);
  not not_25 (not_25_out, E1);
  not not_26 (not_26_out, E2);
  and and_7 (and_7_out, not_26_out, not_27_out);
  not not_27 (not_27_out, E0);
  and and_8 (and_8_out, E1, not_28_out);
  not not_28 (not_28_out, E0);
  and and_9 (and_9_out, E3, E1);
  and and_10 (and_10_out, E3, E2);
  not not_29 (not_29_out, E1);
  not not_30 (not_30_out, E0);
  not not_31 (not_31_out, E3);
  and and_11 (and_11_out, not_31_out, E2);
  not not_32 (not_32_out, E1);
  not not_33 (not_33_out, E2);
  and and_12 (and_12_out, not_33_out, E1);
  and and_13 (and_13_out, E1, not_34_out);
  not not_34 (not_34_out, E0);
  not not_35 (not_35_out, E3);
  and and_14 (and_14_out, not_35_out, E2);
  not not_36 (not_36_out, E1);
  not not_37 (not_37_out, E2);
  and and_15 (and_15_out, not_1_out, not_2_out);
  and and_16 (and_16_out, not_3_out, E1);
  and and_17 (and_17_out, not_4_out, E2);
  and and_18 (and_18_out, E2, E1);
  and and_19 (and_19_out, and_1_out, not_6_out);
  not not_38 (not_38_out, E0);
  and and_20 (and_20_out, not_7_out, not_8_out);
  and and_21 (and_21_out, and_2_out, not_11_out);
  not not_39 (not_39_out, E2);
  not not_40 (not_40_out, E0);
  and and_22 (and_22_out, not_12_out, E1);
  and and_23 (and_23_out, E3, not_13_out);
  or or_1 (or_1_out, and_3_out, and_4_out);
  and and_24 (and_24_out, not_17_out, E0);
  and and_25 (and_25_out, not_18_out, E2);
  and and_26 (and_26_out, E3, not_19_out);
  and and_27 (and_27_out, and_5_out, not_22_out);
  and and_28 (and_28_out, and_6_out, E0);
  and and_29 (and_29_out, E2, not_24_out);
  and and_30 (and_30_out, E2, E1);
  not not_41 (not_41_out, E0);
  and and_31 (and_31_out, E3, not_25_out);
  not not_42 (not_42_out, E0);
  or or_2 (or_2_out, and_7_out, and_8_out);
  or or_3 (or_3_out, and_9_out, and_10_out);
  and and_32 (and_32_out, not_29_out, not_30_out);
  and and_33 (and_33_out, and_11_out, not_32_out);
  not not_43 (not_43_out, E0);
  not not_44 (not_44_out, E2);
  or or_4 (or_4_out, and_12_out, and_13_out);
  and and_34 (and_34_out, and_14_out, not_36_out);
  and and_35 (and_35_out, E3, not_37_out);
  and and_36 (and_36_out, E3, E0);
  or or_5 (or_5_out, and_15_out, and_16_out);
  and and_37 (and_37_out, and_17_out, E0);
  or or_6 (or_6_out, and_18_out, and_19_out);
  and and_38 (and_38_out, E3, not_38_out);
  or or_7 (or_7_out, and_20_out, and_21_out);
  and and_39 (and_39_out, not_39_out, not_40_out);
  and and_40 (and_40_out, and_22_out, E0);
  and and_41 (and_41_out, and_23_out, E0);
  or or_8 (or_8_out, or_1_out, and_24_out);
  or or_9 (or_9_out, and_25_out, and_26_out);
  or or_10 (or_10_out, and_27_out, and_28_out);
  and and_42 (and_42_out, and_29_out, E0);
  and and_43 (and_43_out, and_30_out, not_41_out);
  and and_44 (and_44_out, and_31_out, not_42_out);
  or or_11 (e, or_2_out, or_3_out);
  or or_12 (or_12_out, and_32_out, and_33_out);
  and and_45 (and_45_out, E2, not_43_out);
  and and_46 (and_46_out, E3, not_44_out);
  and and_47 (and_47_out, E3, E1);
  or or_13 (or_13_out, or_4_out, and_34_out);
  or or_14 (or_14_out, and_35_out, and_36_out);
  or or_15 (or_15_out, or_5_out, and_37_out);
  or or_16 (or_16_out, or_6_out, and_38_out);
  or or_17 (or_17_out, or_7_out, and_39_out);
  or or_18 (or_18_out, and_40_out, and_41_out);
  or or_19 (c, or_8_out, or_9_out);
  or or_20 (or_20_out, or_10_out, and_42_out);
  or or_21 (or_21_out, and_43_out, and_44_out);
  or or_22 (or_22_out, or_12_out, and_45_out);
  or or_23 (or_23_out, and_46_out, and_47_out);
  or or_24 (g, or_13_out, or_14_out);
  or or_25 (a, or_15_out, or_16_out);
  or or_26 (b, or_17_out, or_18_out);
  or or_27 (d, or_20_out, or_21_out);
  or or_28 (f, or_22_out, or_23_out);
endmodule
